// Logisim project posit_mult.circ as structural Verilog: 1 circuit, main circuit main
module main (
  input  in_1,
  input  [4:0] in_2,
  input  in_3,
  input  [4:0] in_4,
  output [4:0] out_5,
  output [4:0] out_6,
  output [11:0] out_7,
  output [11:0] out_8,
  output [11:0] out_9,
  output [11:0] out_10,
  output sign_bit,
  output exp_augment,
  output fraction,
  output [9:0] out_14
);

  wire and_2_out, and_4_out, and_5_out, and_6_out, and_7_out, and_8_out, and_9_out, and_10_out, and_13_out,
       and_15_out, and_16_out, and_17_out, and_18_out, and_19_out, and_20_out, and_21_out, nor_1_out,
       not_1_out, not_2_out, not_3_out, not_4_out, or_1_out, or_6_out;
  wire [4:0] negator_1_out, negator_2_out;
  wire [9:0] and_23_out, and_24_out, bit_extender_1_out, bit_extender_2_out;
  wire [10:10] nor_2_out;
  wire [11:5] and_22_out;

  or or_1 (or_1_out, negator_1_out[4], negator_1_out[3], negator_1_out[2], negator_1_out[1], negator_1_out[0]);
  and and_1 (out_9[10], in_3, negator_1_out[4]);
  and and_2 (and_2_out, in_2[4], not_1_out);
  and and_3 (out_9[11], or_1_out, in_3);
  or or_2 (out_9[9], and_2_out, and_5_out);
  Negator #(.width(5)) negator_1 (.in(in_2), .out(negator_1_out));
  and and_4 (and_4_out, in_3, negator_1_out[2]);
  and and_5 (and_5_out, in_3, negator_1_out[3]);
  and and_6 (and_6_out, in_2[2], not_1_out);
  and and_7 (and_7_out, in_2[3], not_1_out);
  or or_3 (out_9[7], and_6_out, and_9_out);
  or or_4 (out_9[8], and_7_out, and_4_out);
  and and_8 (and_8_out, in_3, negator_1_out[0]);
  and and_9 (and_9_out, in_3, negator_1_out[1]);
  and and_10 (and_10_out, in_2[1], not_1_out);
  and and_11 (out_9[5], in_2[0], not_1_out);
  or or_5 (out_9[6], and_10_out, and_8_out);
  not not_1 (not_1_out, in_3);
  xor xor_1 (fraction, sign_bit, out_10[11]);
  Multiplier #(.width(5)) multiplier_1 (.a(in_4), .b(in_2), .out(out_6), .cout(out_5));  // open: cin
  not not_2 (not_2_out, fraction);
  assign bit_extender_1_out = {{9{not_2_out}}, not_2_out};  // Bit_Extender bit_extender_1
  assign bit_extender_2_out = {{9{fraction}}, fraction};  // Bit_Extender bit_extender_2
  Negator #(.width(5)) negator_2 (.in(in_4), .out(negator_2_out));
  or or_6 (or_6_out, negator_2_out[0], negator_2_out[1], negator_2_out[2], negator_2_out[3], negator_2_out[4]);
  and and_12 (and_22_out[11], or_6_out, in_1);
  Adder #(.width(12)) adder_1 (
    .a({2'b00, out_5, out_6}), .b({out_9[11:5], {5{1'b0}}}), .out(out_8));  // open: cin, cout
  nor nor_1 (nor_1_out, out_10[11], out_10[10]);
  and and_13 (and_13_out, in_1, negator_2_out[3]);
  and and_14 (and_22_out[10], in_1, negator_2_out[4]);
  and and_15 (and_15_out, in_4[3], not_3_out);
  and and_16 (and_16_out, in_4[4], not_3_out);
  or or_7 (and_22_out[9], and_16_out, and_13_out);
  or or_8 (and_22_out[8], and_15_out, and_17_out);
  and and_17 (and_17_out, in_1, negator_2_out[2]);
  and and_18 (and_18_out, in_1, negator_2_out[1]);
  and and_19 (and_19_out, in_4[2], not_3_out);
  and and_20 (and_20_out, in_4[1], not_3_out);
  or or_9 (and_22_out[7], and_19_out, and_18_out);
  or or_10 (and_22_out[6], and_20_out, and_21_out);
  not not_3 (not_3_out, in_1);
  and and_21 (and_21_out, in_1, negator_2_out[0]);
  and and_22 (and_22_out[5], in_4[0], not_3_out);
  Adder #(.width(12)) adder_2 (.a({and_22_out, {5{1'b0}}}), .b(out_8), .out(out_7));  // open: cin, cout
  assign and_23_out = out_10[9:0] & bit_extender_1_out;  // AND_Gate and_23, 10 bits wide
  assign and_24_out = out_10[10:1] & bit_extender_2_out;  // AND_Gate and_24, 10 bits wide
  not not_4 (not_4_out, sign_bit);
  assign out_14 = and_23_out | and_24_out;  // OR_Gate or_11, 10 bits wide
  xor xor_2 (sign_bit, in_1, in_3);
  nor nor_2 (nor_2_out[10], in_1, in_3);
  and and_25 (exp_augment, not_4_out, nor_1_out);
  Adder #(.width(12)) adder_3 (.a({sign_bit, nor_2_out[10], {10{1'b0}}}), .b(out_7), .out(out_10));  // open: cin, cout

  assign out_9[4:0] = {5{1'b0}};

  // Notes on the sheet:
  //   Left Frac/Right Hidden preparer
  //   shift selector
  //   core fraction multiplier
  //   concatenation
  //   Right Frac/Left Hidden preparer
  //   ignore top 2 bits
  //   ignore top bit
  //   Hidden Bit Unit
endmodule
